// Logisim project data_path.circ as structural Verilog: 1 circuit, main circuit main
module main (
);

  wire clock_1_out, jalr, pc_src;
  wire [4:0] bit_lower;
  wire [10:0] bit_upper;
  wire [15:0] imm_16bit;
  wire [19:0] pc_inc, pc_next;
  wire [31:0] RA;

  Clock clock_1 (.out(clock_1_out));
  // Reg_file reg_file_1: pin names not known
  pc_circut_main main_1 (
    .pc_src(pc_src), .next_pc(pc_next), .out_9(pc_inc), .Lower5(bit_lower), .upper11(bit_upper),
    .IMM16(imm_16bit), .in_3(clock_1_out), .RS1(RA), .jalr(jalr));
endmodule
